# Fritzing sketch System_Schematic (saved by Fritzing 0.8.7b)
breadboards: 1
perfboards: 1

parts:
  Raspberry_Pi_1 = Raspberry Pi 3
  IC1 = MCP3008 8-channel 10-bit ADC [part_number=MCP3008]
  DHT1 = DHT11 Humitidy and Temperature Sensor
  DHT2 = DHT11 Humitidy and Temperature Sensor
  PART1 = SparkFun Soil Moisture Sensor [part_number=SEN-13322]

nets:
  3V3: Raspberry_Pi_1.3v3, IC1.no_name_yet#15, IC1.no_name_yet#16, PART1.VCC
  GND: Raspberry_Pi_1.GND, IC1.no_name_yet#9, IC1.no_name_yet#14, DHT1.GND, DHT2.GND, PART1.GND
  N1: Raspberry_Pi_1.GIPO17, DHT1.DATA
  N2: Raspberry_Pi_1.GIPO10, IC1.no_name_yet#11
  N3: Raspberry_Pi_1.GIPO9, IC1.no_name_yet#12
  N4: Raspberry_Pi_1.GIPO11, IC1.no_name_yet#13
  N5: Raspberry_Pi_1.GIPO26, DHT2.DATA
  N6: Raspberry_Pi_1.GIPO8, IC1.no_name_yet#10
  VDD: Raspberry_Pi_1.5V, DHT1.VDD, DHT2.VDD
  N7: IC1.no_name_yet#3, PART1.SIG

notes:
  Outdoor Temperature Sensor Signal, GPIO26
  GND
  +5V VCC
  +3V3 VCC
  Analog Signal, ADC Channel 2
  Indoor Temperature Sensor Signal, GPIO17
  Color Key:
  Yellow: Signal
  Red: +5V VCC
  Black: GND
  Green: +3V3 VCC
  Pink: SPI MISO
  Blue: SPI CLK
  Cyan: SPI SS
  Purple: SPI MOSI
  Outdoor Sensor
  Indoor Sensor

custom parts:
  DHT11 Humitidy and Temperature Sensor: DHT11 Humidity and Temperature Sensor
  SparkFun Soil Moisture Sensor: The SparkFun Soil Moisture Sensor is a simple breakout for measuring the moisture in soil and similar materials.
